// Logisim project LC-3.circ as structural Verilog: 16 circuits, main circuit main
module main (
  input  Reset,
  output out_2,
  output out_3,
  output out_4,
  output out_5,
  output out_6,
  output out_7,
  output out_8,
  output [15:0] out_9,
  output [15:0] out_10,
  output [15:0] out_11,
  output [15:0] out_12,
  output [15:0] out_13,
  output [15:0] out_14,
  output [15:0] out_15,
  output [15:0] out_16,
  output [15:0] out_17,
  output halt,
  output [15:0] out_19,
  output [15:0] out_20,
  output [15:0] out_21,
  output [15:0] out_22
);

  wire decodeir_1_p5, getcst_1_usecst, or16_1_out_2, or16_2_out_2, ramctrl_1_memload, ramctrl_1_memstore;
  wire [2:0] nzp_1_nzp;
  wire [15:0] alu_1_output, getcst_1_cst, RegIN, registres_1_out_sr1, registres_1_out_sr2;

  BiClock biclock_1 (.reset(Reset), .signal0(out_2), .signal1(out_3));
  RegPC regpc_1 (
    .H(out_3), .PC(out_9), .Reset(Reset), .IR(out_10), .R(registres_1_out_sr1), .TestNZP(out_5), .Jump(out_4));
  // Probe on out_9
  // Probe on out_11
  GetAddr getaddr_1 (.PC(out_9), .R(registres_1_out_sr1), .IR(out_10), .Addr(out_11), .Fetch(out_2));
  // Probe on out_12
  LED led_1 (.in(out_6));
  RamCtrl ramctrl_1 (
    .Store(out_7), .Fetch(out_2), .Exec(out_3), .Load(out_6), .MemStore(ramctrl_1_memstore),
    .MemLoad(ramctrl_1_memload));
  LED led_2 (.in(out_7));
  // Probe on out_13
  RAM #(.addrWidth(16), .dataWidth(16), .bus("separate")) ram_1 (
    .addr(out_11), .din(out_12), .data(out_13), .str(ramctrl_1_memstore), .clk(ramctrl_1_memstore),
    .ld(ramctrl_1_memload));  // open: sel, clr
  Register #(.width(16), .trigger("falling")) RegIR (.D(out_13), .Q(out_10), .clk(out_2));  // open: en, clr
  // DecodeIR decodeir_1: pin names not known; wires that end beside it: out_6, out_7, out_4, out_10, decodeir_1_p5
  // Probe on out_10[11:9]
  // Probe on out_10[8:6]
  // Probe on out_10[2:0]
  // Probe on getcst_1_cst
  GetCst getcst_1 (.IR(out_10), .Cst(getcst_1_cst), .UseCst(getcst_1_usecst));
  // Probe on out_10[15:14]
  and and_1 (out_8, decodeir_1_p5, out_3);
  Registres registres_1 (
    .SR1(out_10[8:6]), .IN(RegIN), .SR2(out_10[2:0]), .WriteReg(out_8), .DR_SR(out_10[11:9]),
    .OUT_SR1(registres_1_out_sr1), .OUT_SR2(registres_1_out_sr2), .OUT_SR(out_12), .R0(out_14), .R1(out_15),
    .R2(out_16), .R3(out_17), .R4(out_19), .R5(out_20), .R6(out_21), .R7(out_22));
  // Probe on registres_1_out_sr1
  ALU alu_1 (
    .UseCst(getcst_1_usecst), .e2(out_10[15:14]), .Input1(registres_1_out_sr1), .Input2(registres_1_out_sr2),
    .Cst(getcst_1_cst), .Output(alu_1_output), .IR(out_10));
  // Probe on registres_1_out_sr2
  // Probe on alu_1_output
  NZP nzp_1 (.RES(RegIN), .NZP(nzp_1_nzp), .IR(out_10), .WriteReg(out_8), .TestNZP(out_5));
  // Probe on nzp_1_nzp
  Or16 or16_1 (.in_1(out_10), .out_2(or16_1_out_2));
  Or16 or16_2 (.in_1(out_9), .out_2(or16_2_out_2));
  // Probe on out_14
  // Probe on out_15
  // Probe on out_16
  // Probe on out_17
  // Probe on out_19
  // Probe on out_20
  // Probe on out_21
  // Probe on out_22
  and and_2 (halt, ~or16_1_out_2, or16_2_out_2);  // AND_Gate
  RegOp REgOp (.PC(out_9), .IR(out_10), .RegOut(RegIN), .Memory(out_13), .IN(alu_1_output));
  // Probe on RegIN

  // Other names for the same wires on the sheet: Addr[15:0] = out_11; Condition = out_5; Exec = out_3; Fetch = out_2;
  //   IR[15:0] = out_10; JumpInstr = out_4; Load = out_6; MemIN[15:0] = out_12; MemOUT[15:0] = out_13;
  //   PC[15:0] = out_9; R0[15:0] = out_14; R1[15:0] = out_15; R2[15:0] = out_16; R3[15:0] = out_17; R4[15:0] = out_19;
  //   R5[15:0] = out_20; R6[15:0] = out_21; R7[15:0] = out_22; Store = out_7; WriteReg = out_8

  // Notes on the sheet:
  //   R
  //   IR
  //   R
  //   IR
  //   RAM
  //   Traces (NE PAS MODIFIER)______________________________________________________________________________________________________
  //   GetRegs
  //   GetOp
  //   Arret des traces au 1er NOP
endmodule

module ALU (
  input  [15:0] Input1,
  input  [15:0] Input2,
  input  [15:0] Cst,
  input  UseCst,
  input  [1:0] e2,
  input  [15:0] IR,
  output [15:0] Output
);

  wire [3:0] bitselector_1_out, bitselector_2_out;
  wire [15:0] adder_1_out, and_1_out, and_2_out, demultiplexer_1_out0, demultiplexer_2_out0,
       multiplexer_1_out, multiplexer_3_out, not_1_out, not_2_out, subtractor_1_out;

  Multiplexer #(.width(16), .enable("false")) multiplexer_1 (
    .in0(Input2), .in1(Cst), .out(multiplexer_1_out), .sel(UseCst));
  Adder #(.width(16)) adder_1 (.a(multiplexer_1_out), .b(Input1), .out(adder_1_out));  // open: cin, cout
  assign and_1_out = Input1 & multiplexer_1_out;  // AND_Gate and_1, 16 bits wide
  Multiplexer #(.select(2), .width(16), .enable("false")) multiplexer_2 (
    .in0(adder_1_out), .in1(and_1_out), .in2(not_1_out), .in3(multiplexer_3_out), .out(Output), .sel(e2));
  assign not_1_out = ~Input1;  // NOT_Gate not_1, 16 bits wide
  Multiplexer #(.width(16), .enable("false")) multiplexer_3 (
    .in0(subtractor_1_out), .in1(and_2_out), .out(multiplexer_3_out), .sel(IR[4]));
  BitSelector #(.width(16), .group(4)) bitselector_1 (.in(multiplexer_1_out), .out(bitselector_1_out), .sel(2'b00));
  Demultiplexer #(.select(4), .enable("false")) demultiplexer_1 (
    .out0(demultiplexer_1_out0[0]), .out1(demultiplexer_1_out0[1]), .out2(demultiplexer_1_out0[2]),
    .out3(demultiplexer_1_out0[3]), .out4(demultiplexer_1_out0[4]), .out5(demultiplexer_1_out0[5]),
    .out6(demultiplexer_1_out0[6]), .out7(demultiplexer_1_out0[7]), .out8(demultiplexer_1_out0[8]),
    .out9(demultiplexer_1_out0[9]), .out10(demultiplexer_1_out0[10]), .out11(demultiplexer_1_out0[11]),
    .out12(demultiplexer_1_out0[12]), .out13(demultiplexer_1_out0[13]), .out14(demultiplexer_1_out0[14]),
    .out15(demultiplexer_1_out0[15]), .in(1'b1), .sel(bitselector_1_out));
  BitSelector #(.width(16), .group(4)) bitselector_2 (.in(multiplexer_1_out), .out(bitselector_2_out), .sel(2'b00));
  Demultiplexer #(.select(4), .enable("false")) demultiplexer_2 (
    .out0(demultiplexer_2_out0[0]), .out1(demultiplexer_2_out0[1]), .out2(demultiplexer_2_out0[2]),
    .out3(demultiplexer_2_out0[3]), .out4(demultiplexer_2_out0[4]), .out5(demultiplexer_2_out0[5]),
    .out6(demultiplexer_2_out0[6]), .out7(demultiplexer_2_out0[7]), .out8(demultiplexer_2_out0[8]),
    .out9(demultiplexer_2_out0[9]), .out10(demultiplexer_2_out0[10]), .out11(demultiplexer_2_out0[11]),
    .out12(demultiplexer_2_out0[12]), .out13(demultiplexer_2_out0[13]), .out14(demultiplexer_2_out0[14]),
    .out15(demultiplexer_2_out0[15]), .in(1'b1), .sel(bitselector_2_out));
  Subtractor #(.width(16)) subtractor_1 (
    .a(Input1), .b(demultiplexer_1_out0), .out(subtractor_1_out));  // open: bin, bout
  // Probe on subtractor_1_out
  assign not_2_out = ~demultiplexer_2_out0;  // NOT_Gate not_2, 16 bits wide
  // Probe on Input1
  // Probe on not_2_out
  assign and_2_out = Input1;  // AND_Gate and_2, 16 bits wide AND_Gate
  // Probe on and_2_out
endmodule

module BiClock (
  input  reset,
  output signal0,
  output signal1
);

  wire and_1_out, horloge_out, not_1_out, register_1_q;

  Clock horloge (.out(horloge_out));
  not not_1 (not_1_out, register_1_q);
  Register #(.width(1), .trigger("falling")) register_1 (
    .D(not_1_out), .Q(register_1_q), .clk(horloge_out), .clr(reset));  // open: en
  and and_1 (and_1_out, horloge_out, ~reset);  // AND_Gate
  and and_2 (signal0, ~register_1_q, and_1_out);  // AND_Gate
  and and_3 (signal1, register_1_q, and_1_out);

  // Notes on the sheet:
  //   Ce module divise une horloge en deux sous-horloges alternées
  //   Chronogrammes :
  //   horloge: 0101010101 signal0: 0100010001 signal1: 000100010
  //   registre 1-bit
  //   Enable
  //   select : 0 / 1
endmodule

module DecodeIR (
  input  [15:0] IR,
  output Store,
  output WriteReg,
  output Load,
  output Jump
);

  wire ALU_out, LD_out, or_1_out, TB_out;

  and LD (LD_out, IR[13], ~IR[12]);  // AND_Gate
  and JMP (Jump, ~IR[13], ~IR[12]);  // AND_Gate
  and ALU (ALU_out, ~IR[13], IR[12]);  // AND_Gate
  and ST (Store, IR[13], IR[12]);
  and TB (TB_out, IR[15], IR[14], ~IR[13], IR[12]);  // AND_Gate
  // Probe on or_1_out
  or or_1 (or_1_out, ALU_out, TB_out);
  or or_2 (WriteReg, ALU_out, LD_out, TB_out);
  or or_3 (Load, LD_out, TB_out);

  // Notes on the sheet:
  //   Types d'instructions
  //   Instruction modifiant les registres
endmodule

module GetAddr (
  input  [15:0] PC,
  input  [15:0] R,
  input  [15:0] IR,
  input  Fetch,
  output [15:0] Addr
);

  wire and_1_out, LD_out, not_1_out;
  wire [1:0] or_1_out;
  wire [15:0] adder_1_out, adder_2_out, adder_3_out, offset6_1_off6, offset9_1_off9;

  Adder #(.width(16)) adder_1 (.a(PC), .b(16'h1), .out(adder_1_out));  // open: cin, cout
  Offset9 offset9_1 (.IR(IR), .Off9(offset9_1_off9));
  not not_1 (not_1_out, Fetch);
  Adder #(.width(16)) adder_2 (.a(adder_1_out), .b(offset9_1_off9), .out(adder_2_out));  // open: cin, cout
  Offset6 offset6_1 (.IR(IR), .Off6(offset6_1_off6));
  Adder #(.width(16)) adder_3 (.a(R), .b(offset6_1_off6), .out(adder_3_out));  // open: cin, cout
  and and_1 (and_1_out, IR[13], not_1_out);
  // Probe on adder_2_out
  Multiplexer #(.select(2), .width(16), .enable("false")) multiplexer_1 (
    .in0(PC), .in1(adder_2_out), .in3(adder_3_out), .out(Addr), .sel(or_1_out));  // open: in2
  // Probe on or_1_out
  or or_1 (or_1_out[0], LD_out, or_1_out[1]);
  and LDR (or_1_out[1], ~IR[15], IR[14], and_1_out);  // AND_Gate
  and LD (LD_out, ~IR[15], ~IR[14], and_1_out);  // AND_Gate

  // Notes on the sheet:
  //   Adresse Memoire
endmodule

module GetCst (
  input  [15:0] IR,
  output [15:0] Cst,
  output UseCst
);

  assign Cst = {{11{IR[4]}}, IR[4:0]};  // Bit_Extender bit_extender_1

  assign UseCst = IR[5];
endmodule

module NZP (
  input  [15:0] RES,
  input  WriteReg,
  input  [15:0] IR,
  output [2:0] NZP,
  output TestNZP
);

  wire and_2_out, and_3_out, and_4_out, not_2_out, or16_1_out_2;
  wire [1:0] and_1_out;

  not not_1 (and_1_out[1], or16_1_out_2);
  Or16 or16_1 (.in_1(RES), .out_2(or16_1_out_2));
  not not_2 (not_2_out, RES[15]);
  and and_1 (and_1_out[0], not_2_out, ~and_1_out[1]);  // AND_Gate
  // Probe on {RES[15], and_1_out}
  verrou3 verrou3_1 (.in_1(WriteReg), .in_2({RES[15], and_1_out}), .out_3(NZP));
  and and_2 (and_2_out, NZP[0], IR[9]);
  and and_3 (and_3_out, NZP[2], IR[11]);
  and and_4 (and_4_out, NZP[1], IR[10]);
  or or_1 (TestNZP, and_2_out, and_4_out, and_3_out);

  // Notes on the sheet:
  //   (Resultat du calcul courant)
  //   (Instruction mettant à jour NZP)
  //   (Instruction courante)
  //   Test de saut
  //   Valeur actuel du registre d'état NZP
  //   (pour l'instant toujours 000)
endmodule

// Off6
module Offset6 (
  input  [15:0] IR,
  output [15:0] Off6
);

  assign Off6 = {{10{IR[5]}}, IR[5:0]};  // Bit_Extender bit_extender_1
endmodule

// Off9
module Offset9 (
  input  [15:0] IR,
  output [15:0] Off9
);

  assign Off9 = {{7{IR[8]}}, IR[8:0]};  // Bit_Extender bit_extender_1
endmodule

module Or16 (
  input  [15:0] in_1,
  output out_2
);

  wire [3:0] or_1_out;

  assign or_1_out = in_1[3:0] | in_1[7:4] | in_1[11:8] | in_1[15:12];  // OR_Gate or_1, 4 bits wide
  or or_2 (out_2, or_1_out[0], or_1_out[1], or_1_out[2], or_1_out[3]);
endmodule

module RamCtrl (
  input  Exec,
  input  Fetch,
  input  Load,
  input  Store,
  output MemLoad,
  output MemStore
);

  wire and_1_out;

  and and_1 (and_1_out, Exec, Load);
  and and_2 (MemStore, Exec, Store);
  or or_1 (MemLoad, Fetch, and_1_out);
endmodule

module Registres (
  input  [2:0] SR1,
  input  [15:0] IN,
  input  [2:0] SR2,
  input  WriteReg,
  input  [2:0] DR_SR,
  output [15:0] R0,
  output [15:0] OUT_SR1,
  output [15:0] R1,
  output [15:0] R2,
  output [15:0] R3,
  output [15:0] OUT_SR2,
  output [15:0] R4,
  output [15:0] R5,
  output [15:0] OUT_SR,
  output [15:0] R6,
  output [15:0] R7
);

  wire decoder_1_out0, decoder_1_out1, decoder_1_out2, decoder_1_out3, decoder_1_out4, decoder_1_out5,
       decoder_1_out6, decoder_1_out7;

  Decoder #(.select(3), .disabled(0)) decoder_1 (
    .out0(decoder_1_out0), .out1(decoder_1_out1), .out2(decoder_1_out2), .out3(decoder_1_out3),
    .out4(decoder_1_out4), .out5(decoder_1_out5), .out6(decoder_1_out6), .out7(decoder_1_out7), .sel(DR_SR),
    .en(WriteReg));
  Register #(.width(16), .trigger("falling")) u_R0 (.D(IN), .Q(R0), .clk(decoder_1_out0));  // open: en, clr
  Register #(.width(16), .trigger("falling")) u_R1 (.D(IN), .Q(R1), .clk(decoder_1_out1));  // open: en, clr
  Register #(.width(16), .trigger("falling")) u_R2 (.D(IN), .Q(R2), .clk(decoder_1_out2));  // open: en, clr
  Register #(.width(16), .trigger("falling")) u_R3 (.D(IN), .Q(R3), .clk(decoder_1_out3));  // open: en, clr
  Register #(.width(16), .trigger("falling")) u_R4 (.D(IN), .Q(R4), .clk(decoder_1_out4));  // open: en, clr
  Register #(.width(16), .trigger("falling")) u_R5 (.D(IN), .Q(R5), .clk(decoder_1_out5));  // open: en, clr
  Register #(.width(16), .trigger("falling")) u_R6 (.D(IN), .Q(R6), .clk(decoder_1_out6));  // open: en, clr
  Register #(.width(16), .trigger("falling")) u_R7 (.D(IN), .Q(R7), .clk(decoder_1_out7));  // open: en, clr
  Multiplexer #(.select(3), .width(16), .enable("false")) multiplexer_1 (
    .in0(R0), .in1(R1), .in2(R2), .in3(R3), .in4(R4), .in5(R5), .in6(R6), .in7(R7), .out(OUT_SR1), .sel(SR1));
  Multiplexer #(.select(3), .width(16), .enable("false")) multiplexer_2 (
    .in0(R0), .in1(R1), .in2(R2), .in3(R3), .in4(R4), .in5(R5), .in6(R6), .in7(R7), .out(OUT_SR2), .sel(SR2));
  Multiplexer #(.select(3), .width(16), .enable("false")) multiplexer_3 (
    .in0(R0), .in1(R1), .in2(R2), .in3(R3), .in4(R4), .in5(R5), .in6(R6), .in7(R7), .out(OUT_SR), .sel(DR_SR));
endmodule

module RegPC (
  input  [15:0] R,
  input  Jump,
  input  H,
  input  Reset,
  input  [15:0] IR,
  input  TestNZP,
  output [15:0] PC
);

  wire and_3_out;
  wire [1:0] and_1_out;
  wire [15:0] adder_1_out, adder_2_out, multiplexer_1_out, offset9_1_off9;

  Offset9 offset9_1 (.IR(IR), .Off9(offset9_1_off9));
  and and_1 (and_1_out[0], Jump, IR[15], IR[14]);
  and and_2 (and_1_out[1], Jump, TestNZP, and_3_out);
  and and_3 (and_3_out, ~IR[14], ~IR[15]);  // AND_Gate
  Adder #(.width(16)) adder_1 (.a(adder_2_out), .b(offset9_1_off9), .out(adder_1_out));  // open: cin, cout
  // Probe on and_1_out
  Adder #(.width(16)) adder_2 (.a(PC), .b({16{1'b0}}), .out(adder_2_out), .cin(1'b1));  // open: cout
  Multiplexer #(.select(2), .width(16), .enable("false")) multiplexer_1 (
    .in0(adder_2_out), .in1(R), .in2(adder_1_out), .out(multiplexer_1_out), .sel(and_1_out));  // open: in3
  Register #(.width(16), .trigger("falling")) u_PC (.D(multiplexer_1_out), .Q(PC), .clk(H), .clr(Reset));  // open: en

  // Notes on the sheet:
  //   PC <- PC + 1
endmodule

module RegOp (
  input  [15:0] IN,
  input  [15:0] Memory,
  input  [15:0] PC,
  input  [15:0] IR,
  output [15:0] RegOut
);

  wire [1:0] LD_out;
  wire [15:0] adder_1_out, adder_2_out, offset9_1_off9, undriven;

  Offset9 offset9_1 (.IR(IR), .Off9(offset9_1_off9));
  Adder #(.width(16)) adder_1 (.a(PC), .b(16'h1), .out(adder_1_out));  // open: cin, cout
  Adder #(.width(16)) adder_2 (.a(adder_1_out), .b(offset9_1_off9), .out(adder_2_out));  // open: cin, cout
  and LD (LD_out[0], IR[13], ~IR[12]);  // AND_Gate
  Multiplexer #(.select(3), .width(16), .enable("false")) multiplexer_1 (
    .in0(IN), .in1(Memory), .in2(adder_1_out), .in3(adder_2_out), .in6(undriven), .in7(undriven),
    .out(RegOut), .sel({1'b0, LD_out}));  // open: in4, in5
  and LEA (LD_out[1], IR[15], IR[14], LD_out[0]);
  // Probe on {1'b0, LD_out}

  // Notes on the sheet:
  //   (Ancienne branche non utilisée)
endmodule

module verrou (
  input  in_1,
  input  in_2,
  output out_3
);

  wire and_1_out, and_2_out, not_1_out, not_2_out, not_3_out, or_1_out;

  not not_1 (not_1_out, in_2);
  and and_1 (and_1_out, in_1, not_1_out);
  and and_2 (and_2_out, in_1, in_2);
  or or_1 (or_1_out, and_1_out, not_2_out);
  not not_2 (not_2_out, out_3);
  not not_3 (not_3_out, or_1_out);
  or or_2 (out_3, not_3_out, and_2_out);
endmodule

module verrou3 (
  input  in_1,
  input  [2:0] in_2,
  output [2:0] out_3
);

  verrou verrou_1 (.in_1(in_1), .in_2(in_2[0]), .out_3(out_3[0]));
  verrou verrou_2 (.in_1(in_1), .in_2(in_2[1]), .out_3(out_3[1]));
  verrou verrou_3 (.in_1(in_1), .in_2(in_2[2]), .out_3(out_3[2]));
endmodule
